# Fritzing sketch Wiring Diagram (saved by Fritzing 0.9.3b)

parts:
  Part1 = Arduino Uno (Rev3) - ICSP
  A1 = DM860A Stepper Motor Driver
  A2 = DM860A Stepper Motor Driver
  J1 = 2.1mm Barrel Jack with Terminal Block

nets:
  N1: Part1.GND, A1.PUL-(PUL)
  N2: Part1.D2, A1.DIR+(+5V)
  N3: Part1.D3_PWM, A1.PUL+(+5V)
  N4: Part1.D4, A2.DIR+(+5V)
  N5: Part1.D5_PWM, A2.PUL+(+5V)
  N6: A2.VDC, J1.POS-TERM
  N7: A2.GND, J1.NEG-TERM

custom parts:
  DM860A Stepper Motor Driver: DM860A is a type of two-phase hybrid stepping motor driver, The drive voltage of which is from 24VDC to 80VDC. It is designed for use with 2-phase hybrid stepper motor of all kinds with 57mm to 110mm outside diameter and less than 8.0A phase current. Mar 2023: Correct pcb layerId as the part won't save correctly in a .fzz file as is.
